# Fritzing sketch 1MotorPWM (saved by Fritzing 0.9.2b)
breadboards: 1

parts:
  Part1 = Arduino Uno (Rev3)
  IC1 = H-Bridge [package=THT]
  M1 = DC Motor
  BAT1 = BC9VPC [package=bc9vpc]

nets:
  GND: Part1.GND, IC1.GND1, IC1.GND2, BAT1.V-
  N1: Part1.D3_PWM, IC1.2A
  N2: Part1.D4, IC1.1A
  N3: Part1.D5_PWM, IC1.1_2EN
  N4: Part1.5V, IC1.VCC2
  N5: IC1.1Y, M1.pin_2
  N6: IC1.2Y, M1.pin_1
  N7: IC1.VCC1, BAT1.V+
