# Fritzing sketch limitSwitch (saved by Fritzing 0.9.2b)
breadboards: 1

parts:
  Part1 = Arduino Uno (Rev3)
  S1 = Pushbutton [package=THT]
  R1 = Resistor [tolerance=±5% resistance=10k package=THT]

nets:
  N1: Part1.D12/MISO, S1.leg0, R1.Pin_1
  N2: Part1.GND, R1.Pin_0
  N3: Part1.5V, S1.leg1
